// Logisim project microProcessor_bird.circ as structural Verilog: 8 circuits, main circuit main
module main (
  input  [15:0] Key_2,
  input  [15:0] Key_1,
  input  Ready_1,
  input  Ready_2
);

  wire and_1_out, and_2_out, and_3_out, and_4_out, and_5_out, and_6_out, and_7_out, and_8_out, and_9_out,
       clock_1_out, cpu_1_intack, cpu_1_memld, not_1_out, priority_encoder_1_gs, ready_1_readybit,
       ready_2_readybit, timerReady;
  wire [2:0] priority_encoder_1_out, priority_encoder_2_out;
  wire [11:0] cpu_1_addrout;
  wire [15:0] bit_extender_1_out, cpu_1_dout, multiplexer_1_out, multiplexer_2_out, out_2_q, out_q,
       ram_1_data, ram_2_data, ram_3_data, ram_4_data, ram_5_data, timerOUT;

  Clock clock_1 (.out(clock_1_out));
  Ready u_ready_1 (.READYBIT(ready_1_readybit), .Ready_1(Ready_1), .ADDRon(and_1_out), .clock(clock_1_out));
  Ready u_ready_2 (.READYBIT(ready_2_readybit), .Ready_1(Ready_2), .ADDRon(and_2_out), .clock(clock_1_out));
  CPU cpu_1 (
    .MEMLD(cpu_1_memld), .clk(clock_1_out), .ADDROUT(cpu_1_addrout), .Dout(cpu_1_dout),
    .Din(multiplexer_2_out), .INT(priority_encoder_1_gs), .INTACK(cpu_1_intack));
  Priority_Encoder priority_encoder_1 (
    .in1(ready_1_readybit), .in2(ready_2_readybit), .in3(timerReady), .out(priority_encoder_1_out),
    .gs(priority_encoder_1_gs));  // open: in0, in4, in5, in6, in7, en_in, en_out
  Multiplexer #(.select(3), .width(16), .enable("false")) multiplexer_1 (
    .in0({16{1'b0}}), .in1(ram_1_data), .in2(ram_2_data), .in3(ram_3_data), .in4(timerOUT),
    .out(multiplexer_1_out), .sel(priority_encoder_2_out));  // open: in5, in6, in7
  Multiplexer #(.width(16), .enable("false")) multiplexer_2 (
    .in0(multiplexer_1_out), .in1(bit_extender_1_out), .out(multiplexer_2_out), .sel(cpu_1_intack));
  RAM #(.addrWidth(2), .dataWidth(16), .bus("separate")) ram_1 (
    .addr(cpu_1_addrout[1:0]), .din(Key_1), .data(ram_1_data), .clk(clock_1_out));  // open: str, sel, ld, clr
  assign bit_extender_1_out = {{13{1'b0}}, priority_encoder_1_out};  // Bit_Extender bit_extender_1
  RAM #(.addrWidth(2), .dataWidth(16), .bus("separate")) ram_2 (
    .addr(cpu_1_addrout[1:0]), .din(Key_2), .data(ram_2_data), .clk(clock_1_out));  // open: str, sel, ld, clr
  and and_1 (and_1_out, cpu_1_addrout[11], cpu_1_addrout[10], ~cpu_1_addrout[9], ~cpu_1_addrout[8], ~cpu_1_addrout[7], ~cpu_1_addrout[6], ~cpu_1_addrout[5], cpu_1_addrout[4], ~cpu_1_addrout[3], ~cpu_1_addrout[2]);  // AND_Gate
  Priority_Encoder priority_encoder_2 (
    .in0(1'b1), .in1(and_1_out), .in2(and_2_out), .in3(not_1_out), .in4(and_7_out),
    .out(priority_encoder_2_out));  // open: in5, in6, in7, en_in
  and and_2 (and_2_out, cpu_1_addrout[11], cpu_1_addrout[10], ~cpu_1_addrout[9], ~cpu_1_addrout[8], ~cpu_1_addrout[7], ~cpu_1_addrout[6], cpu_1_addrout[5], ~cpu_1_addrout[4], ~cpu_1_addrout[3], ~cpu_1_addrout[2]);  // AND_Gate
  RAM #(.addrWidth(12), .dataWidth(16), .bus("separate")) ram_3 (
    .addr(cpu_1_addrout), .din(cpu_1_dout), .data(ram_3_data), .str(and_3_out), .clk(clock_1_out), .ld(1'b1));  // open: sel, clr
  and and_3 (and_3_out, cpu_1_memld, not_1_out);
  not not_1 (not_1_out, and_4_out);
  and and_4 (and_4_out, cpu_1_addrout[11], cpu_1_addrout[10]);
  and and_5 (and_5_out, and_6_out, cpu_1_memld);
  and and_6 (and_6_out, cpu_1_addrout[11], cpu_1_addrout[10], ~cpu_1_addrout[9], ~cpu_1_addrout[8], ~cpu_1_addrout[7], ~cpu_1_addrout[6], cpu_1_addrout[5], cpu_1_addrout[4], ~cpu_1_addrout[3], ~cpu_1_addrout[2]);  // AND_Gate
  RAM #(.addrWidth(2), .dataWidth(16), .bus("separate")) ram_4 (
    .addr(cpu_1_addrout[1:0]), .din(cpu_1_dout), .data(ram_4_data), .str(and_5_out), .clk(clock_1_out),
    .ld(and_5_out));  // open: sel, clr
  and and_7 (and_7_out, cpu_1_addrout[11], cpu_1_addrout[10], ~cpu_1_addrout[9], ~cpu_1_addrout[8], ~cpu_1_addrout[7], cpu_1_addrout[6], ~cpu_1_addrout[5], ~cpu_1_addrout[4], ~cpu_1_addrout[3], ~cpu_1_addrout[2]);  // AND_Gate
  Register #(.width(16)) out (.D(ram_4_data), .en(and_5_out), .Q(out_q), .clk(clock_1_out));  // open: clr
  Hex_Digit_Display hex_digit_display_1 (.value(out_q[11:8]));  // open: dp
  Hex_Digit_Display hex_digit_display_2 (.value(out_q[15:12]));  // open: dp
  RAM #(.addrWidth(2), .dataWidth(16), .bus("separate")) ram_5 (
    .addr(cpu_1_addrout[1:0]), .din(cpu_1_dout), .data(ram_5_data), .str(and_8_out), .clk(clock_1_out),
    .ld(and_8_out));  // open: sel, clr
  and and_8 (and_8_out, cpu_1_memld, and_9_out);
  and and_9 (and_9_out, cpu_1_addrout[11], cpu_1_addrout[10], ~cpu_1_addrout[9], ~cpu_1_addrout[8], ~cpu_1_addrout[7], cpu_1_addrout[6], ~cpu_1_addrout[5], cpu_1_addrout[4], ~cpu_1_addrout[3], ~cpu_1_addrout[2]);  // AND_Gate
  Hex_Digit_Display hex_digit_display_3 (.value(out_q[3:0]));  // open: dp
  Hex_Digit_Display hex_digit_display_4 (.value(out_q[7:4]));  // open: dp
  TIMER timer_1 (.clk(clock_1_out), .READYFlag(timerReady), .OUT(timerOUT));
  Register #(.width(16)) out_2 (.D(ram_5_data), .en(and_8_out), .Q(out_2_q), .clk(clock_1_out));  // open: clr
  Hex_Digit_Display hex_digit_display_5 (.value(out_2_q[15:12]));  // open: dp
  Hex_Digit_Display hex_digit_display_6 (.value(out_2_q[11:8]));  // open: dp
  Hex_Digit_Display hex_digit_display_7 (.value(out_2_q[7:4]));  // open: dp
  Hex_Digit_Display hex_digit_display_8 (.value(out_2_q[3:0]));  // open: dp

  // Notes on the sheet:
  //   C10 - C13
  //   INPUT1 (4)
  //   C20 - C23
  //   INPUT2 (4)
  //   INPUT1
  //   INPUT2
  //   000 - BFF
  //   PROGRAM MEM (3K) - 12BIT
  //   MEM
  //   OUTPUT
  //   C30 - C33
  //   OUTPUT (4)
  //   C50 (output)
  //   C40
  //   TIMER (4)
endmodule

module regbank (
  input  REGLD,
  input  ZF,
  input  [2:0] REGSEL,
  input  INT,
  input  INTLD,
  input  ZFLD,
  input  [15:0] Din,
  input  SP_minus_minus,
  input  SP_plus_plus,
  input  clock,
  output [15:0] _0,
  output [15:0] _1,
  output [15:0] _2,
  output [15:0] _3,
  output [15:0] _4,
  output [15:0] _5,
  output [15:0] _6,
  output [15:0] _7
);

  wire and_1_out, and_2_out, and_3_out, and_4_out, and_5_out, and_6_out, and_7_out, and_8_out,
       decoder_1_out0, decoder_1_out1, decoder_1_out2, decoder_1_out3, decoder_1_out4, decoder_1_out5,
       decoder_1_out6, decoder_1_out7, or_1_out, or_2_out, or_3_out;

  Decoder #(.select(3)) decoder_1 (
    .out0(decoder_1_out0), .out1(decoder_1_out1), .out2(decoder_1_out2), .out3(decoder_1_out3),
    .out4(decoder_1_out4), .out5(decoder_1_out5), .out6(decoder_1_out6), .out7(decoder_1_out7), .sel(REGSEL));  // open: en
  and and_1 (and_1_out, decoder_1_out0, REGLD);
  and and_2 (and_2_out, decoder_1_out1, REGLD);
  and and_3 (and_3_out, decoder_1_out2, REGLD);
  and and_4 (and_4_out, decoder_1_out3, REGLD);
  and and_5 (and_5_out, decoder_1_out4, REGLD);
  and and_6 (and_6_out, decoder_1_out5, REGLD);
  and and_7 (and_7_out, decoder_1_out6, REGLD);
  and and_8 (and_8_out, decoder_1_out7, REGLD);
  Register #(.width(16)) register_1 (.D(Din), .en(and_1_out), .Q(_0), .clk(clock));  // open: clr
  Register #(.width(16)) register_2 (.D(Din), .en(and_2_out), .Q(_1), .clk(clock));  // open: clr
  Register #(.width(16)) register_3 (.D(Din), .en(and_3_out), .Q(_2), .clk(clock));  // open: clr
  Register #(.width(16)) register_4 (.D(Din), .en(and_4_out), .Q(_3), .clk(clock));  // open: clr
  Register #(.width(16)) register_5 (.D(Din), .en(and_5_out), .Q(_4), .clk(clock));  // open: clr
  Register #(.width(16)) register_6 (.D(Din), .en(and_6_out), .Q(_5), .clk(clock));  // open: clr
  or or_1 (or_1_out, and_8_out, SP_minus_minus);
  or or_2 (or_2_out, SP_minus_minus, SP_plus_plus);
  Counter #(.width(16), .max('hffff)) SP (
    .load(or_1_out), .D(Din), .count(or_2_out), .Q(_7), .clk(clock));  // open: carry, clr
  or or_3 (or_3_out, INTLD, and_7_out, ZFLD);
  Register #(.width(16)) register_7 (.D({{14{1'b0}}, INT, ZF}), .en(or_3_out), .Q(_6), .clk(clock));  // open: clr

  // Notes on the sheet:
  //   load etmek için:
  //   inc etmek için: 
  //   dec etmek için:
  //   Load=1, Counter = 0
  //   Load=0, Counter=1
  //   Load=1, Counter=1
endmodule

module ALU (
  input  [15:0] inputData1,
  input  [15:0] inputData2,
  input  [5:0] ALUOP,
  output ZF,
  output [15:0] RESULT
);

  wire [15:0] adder_1_out, adder_2_out, and_1_out, multiplexer_1_out, not_1_out, or_1_out, subtractor_1_out,
       subtractor_2_out, xor_1_out;

  Adder #(.width(16)) adder_1 (.a(inputData1), .b(inputData2), .out(adder_1_out));  // open: cin, cout
  Subtractor #(.width(16)) subtractor_1 (.a(inputData1), .b(inputData2), .out(subtractor_1_out));  // open: bin, bout
  assign and_1_out = inputData1 & inputData2;  // AND_Gate and_1, 16 bits wide
  assign or_1_out = inputData1 | inputData2;  // OR_Gate or_1, 16 bits wide
  assign xor_1_out = inputData1 ^ inputData2;  // XOR_Gate xor_1, 16 bits wide
  assign not_1_out = ~inputData1;  // NOT_Gate not_1, 16 bits wide
  Adder #(.width(16)) adder_2 (.a(inputData1), .b(16'h1), .out(adder_2_out));  // open: cin, cout
  Subtractor #(.width(16)) subtractor_2 (.a(inputData1), .b(16'h1), .out(subtractor_2_out));  // open: bin, bout
  Multiplexer #(.select(3), .width(16), .enable("false")) multiplexer_1 (
    .in0(not_1_out), .in1(inputData1), .in2(adder_2_out), .in3(subtractor_2_out), .out(multiplexer_1_out),
    .sel(ALUOP[2:0]));  // open: in4, in5, in6, in7
  Multiplexer #(.select(3), .width(16), .enable("false")) multiplexer_2 (
    .in0(adder_1_out), .in1(subtractor_1_out), .in2(and_1_out), .in3(or_1_out), .in4(xor_1_out),
    .in7(multiplexer_1_out), .out(RESULT), .sel(ALUOP[5:3]));  // open: in5, in6
  nor nor_1 (ZF, RESULT[0], RESULT[1], RESULT[2], RESULT[3], RESULT[4], RESULT[5], RESULT[6], RESULT[7], RESULT[8], RESULT[9], RESULT[10], RESULT[11], RESULT[12], RESULT[13], RESULT[14], RESULT[15]);
endmodule

module PC (
  input  PCLD,
  input  PC_INC,
  input  [11:0] JUMPADDR,
  input  clk,
  output [11:0] pc
);

  wire [11:0] adder_1_out, multiplexer_1_out, multiplexer_2_out;

  Multiplexer #(.width(12), .enable("false")) multiplexer_1 (
    .in0(pc), .in1(adder_1_out), .out(multiplexer_1_out), .sel(PC_INC));
  Multiplexer #(.width(12), .enable("false")) multiplexer_2 (
    .in0(multiplexer_1_out), .in1(JUMPADDR), .out(multiplexer_2_out), .sel(PCLD));
  Register #(.width(12)) u_PC (.D(multiplexer_2_out), .Q(pc), .clk(clk));  // open: en, clr
  Adder #(.width(12)) adder_1 (.a(pc), .b(12'h1), .out(adder_1_out));  // open: cin, cout
endmodule

module ControlUnit (
  input  [3:0] opcode,
  input  ZF,
  input  INT,
  input  clk,
  output DATAMUX,
  output IMM,
  output IRLD,
  output MEMLD,
  output MUX,
  output ZFLD,
  output REGLD,
  output [1:0] ADRMUX,
  output PCINC,
  output PCLD,
  output PCMUX,
  output SP_minus_minus,
  output SP_plus_plus
);

  wire [1:1] and_1_out;
  wire [3:0] multiplexer_1_out, multiplexer_2_out, register_1_q, rom_1_data, undriven;
  wire [4:0] bit_extender_1_out;
  wire [18:18] rom_1_data_2;

  and and_1 (and_1_out[1], ~opcode[0], ~opcode[1], opcode[2], ~opcode[3]);  // AND_Gate
  Multiplexer #(.select(2), .width(4), .enable("false")) multiplexer_1 (
    .in0(opcode), .in1(opcode), .in2(4'b0000), .in3(4'b0101), .out(multiplexer_1_out),
    .sel({and_1_out[1], ZF}));
  Multiplexer #(.width(4), .enable("false")) multiplexer_2 (
    .in0(rom_1_data), .in1(multiplexer_1_out), .out(multiplexer_2_out), .sel(rom_1_data_2[18]));
  assign bit_extender_1_out = {{1{1'b0}}, multiplexer_2_out};  // Bit_Extender bit_extender_1
  Multiplexer #(.width(5), .enable("false")) multiplexer_3 (.in0(bit_extender_1_out));  // open: in1, out, sel
  Register #(.width(4)) register_1 (.D(undriven), .Q(register_1_q), .clk(clk));  // open: en, clr
  ROM #(.addrWidth(4), .dataWidth(19)) rom_1 (
    .addr(register_1_q),
    .data({rom_1_data_2[18], SP_plus_plus, SP_minus_minus, PCMUX, PCLD, PCINC, ADRMUX, REGLD, ZFLD, MUX, MEMLD, IRLD, IMM, DATAMUX, rom_1_data}));  // open: sel

  // Notes on the sheet:
  //   contents of rom_1 (hex, n*v repeats v):
  //   42040 2500 d00 880 0 4000 2620 600 11080 2000c 15090 2000d 1500 d000
endmodule

module CPU (
  input  clk,
  input  [15:0] Din,
  input  INT,
  output [11:0] ADDROUT,
  output [15:0] Dout,
  output MEMLD,
  output INTACK
);

  wire alu_1_zf, controlunit_1_datamux, controlunit_1_imm, controlunit_1_irld, controlunit_1_mux,
       controlunit_1_pcinc, controlunit_1_pcld, controlunit_1_pcmux, controlunit_1_regld,
       controlunit_1_sp_minus_minus, controlunit_1_sp_plus_plus, INTLD, ZFLD;
  wire [1:0] controlunit_1_adrmux;
  wire [2:0] IR_q, IR_q_2;
  wire [3:0] adder_2_out_2, undriven_2;
  wire [5:0] IR_q_3;
  wire [11:0] adder_1_out, adder_2_out, multiplexer_1_out, multiplexer_6_out, pc_1_pc, undriven;
  wire [15:0] alu_1_result, bit_extender_1_out, multiplexer_3_out, multiplexer_4_out, multiplexer_7_out,
       regbank_1__0, regbank_1__1, regbank_1__2, regbank_1__3, regbank_1__4, regbank_1__5, regbank_1__6,
       regbank_1__7;
  wire [15:12] multiplexer_6_out_2;

  PC pc_1 (
    .pc(pc_1_pc), .PC_INC(controlunit_1_pcinc), .clk(clk), .PCLD(controlunit_1_pcld),
    .JUMPADDR(multiplexer_1_out));
  Multiplexer #(.width(12), .enable("false")) multiplexer_1 (
    .in0(adder_1_out), .in1(Din[11:0]), .out(multiplexer_1_out), .sel(controlunit_1_pcmux));
  Adder #(.width(12)) adder_1 (.a(pc_1_pc), .b({IR_q_3, IR_q_2, IR_q}), .out(adder_1_out));  // open: cin, cout
  Multiplexer #(.select(2), .width(12), .enable("false")) multiplexer_2 (
    .in0(pc_1_pc), .in1(multiplexer_6_out), .in2(undriven), .in3(adder_2_out), .out(ADDROUT),
    .sel(controlunit_1_adrmux));
  assign bit_extender_1_out = {{4{1'b0}}, pc_1_pc};  // Bit_Extender bit_extender_1
  regbank regbank_1 (
    .REGLD(controlunit_1_regld), .REGSEL(IR_q), .Din(multiplexer_3_out), ._0(regbank_1__0),
    ._1(regbank_1__1), ._2(regbank_1__2), ._3(regbank_1__3), .clock(clk), ._4(regbank_1__4),
    ._5(regbank_1__5), ._6(regbank_1__6), ._7(regbank_1__7), .SP_plus_plus(controlunit_1_sp_minus_minus),
    .SP_minus_minus(controlunit_1_sp_plus_plus), .ZF(alu_1_zf), .INT(INT), .ZFLD(ZFLD), .INTLD(INTLD));
  Multiplexer #(.width(16), .enable("false")) multiplexer_3 (
    .in0(alu_1_result), .in1(Din), .out(multiplexer_3_out), .sel(controlunit_1_mux));
  Multiplexer #(.select(3), .width(16), .enable("false")) multiplexer_4 (
    .in0(regbank_1__0), .in1(regbank_1__1), .in2(regbank_1__2), .in3(regbank_1__3), .in4(regbank_1__4),
    .in5(regbank_1__5), .in6(regbank_1__6), .in7({undriven_2, undriven}), .out(multiplexer_4_out),
    .sel(IR_q_2));
  Multiplexer #(.width(16), .enable("false")) multiplexer_5 (
    .in0(multiplexer_4_out), .in1(bit_extender_1_out), .out(Dout), .sel(controlunit_1_datamux));
  Multiplexer #(.select(3), .width(16), .enable("false")) multiplexer_6 (
    .in0(regbank_1__0), .in1(regbank_1__1), .in2(regbank_1__2), .in3(regbank_1__3), .in4(regbank_1__4),
    .in5(regbank_1__5), .in6(regbank_1__6), .in7(regbank_1__7),
    .out({multiplexer_6_out_2, multiplexer_6_out}), .sel(IR_q_3[2:0]));
  Multiplexer #(.width(16), .enable("false")) multiplexer_7 (
    .in0({multiplexer_6_out_2, multiplexer_6_out}), .in1(Din), .out(multiplexer_7_out),
    .sel(controlunit_1_imm));
  ALU alu_1 (
    .inputData1(multiplexer_4_out), .inputData2(multiplexer_7_out), .ZF(alu_1_zf), .RESULT(alu_1_result),
    .ALUOP(IR_q_3));
  Adder #(.width(16)) adder_2 (.a(Din), .b(16'h950), .out({adder_2_out_2, adder_2_out}));  // open: cin, cout
  Register #(.width(12)) IR (
    .D(Din[11:0]), .en(controlunit_1_irld), .Q({IR_q_3, IR_q_2, IR_q}), .clk(clk));  // open: clr
  ControlUnit controlunit_1 (
    .ZF(regbank_1__6[0]), .IMM(controlunit_1_imm), .IRLD(controlunit_1_irld), .MEMLD(MEMLD),
    .MUX(controlunit_1_mux), .ZFLD(ZFLD), .REGLD(controlunit_1_regld), .ADRMUX(controlunit_1_adrmux),
    .PCINC(controlunit_1_pcinc), .PCLD(controlunit_1_pcld), .opcode(Din[15:12]), .clk(clk),
    .DATAMUX(controlunit_1_datamux), .PCMUX(controlunit_1_pcmux),
    .SP_minus_minus(controlunit_1_sp_minus_minus), .SP_plus_plus(controlunit_1_sp_plus_plus),
    .INT(regbank_1__6[1]));

  // Notes on the sheet:
  //   IDT ADDRESS
endmodule

module Ready (
  input  clock,
  input  ADDRon,
  input  Ready_1,
  output READYBIT
);

  wire and_1_out, not_1_out;

  and and_1 (and_1_out, Ready_1, ADDRon);
  D_Flip_Flop u_ReadyBit (.clk(clock), .Q(READYBIT), .preset(and_1_out), .reset(not_1_out));  // open: D, Qn, en
  not not_1 (not_1_out, and_1_out);
endmodule

module TIMER (
  input  clk,
  output READYFlag,
  output [15:0] OUT
);

  wire [15:0] incrementer_q;

  Counter #(.width(16), .max('hffff)) incrementer (
    .count(clk), .Q(incrementer_q), .clk(clk), .clr(READYFlag));  // open: load, D, carry
  Comparator #(.width(16)) comparator_1 (.a(incrementer_q), .b(16'h1004), .eq(READYFlag));  // open: gt, lt
  Counter #(.width(16), .max('hffff)) incrementer_2 (
    .count(READYFlag), .Q(OUT), .clk(clk));  // open: load, D, carry, clr
endmodule
