// Logisim project microProcessor_frog.circ as structural Verilog: 5 circuits, main circuit main
module main (
);

  wire clock_1_out, controlunit_1_imm, controlunit_1_irld, controlunit_1_ld, controlunit_1_mux,
       controlunit_1_pcinc;
  wire [1:0] ram_1_data, ram_1_data_2;
  wire [3:0] regbank_1__0;
  wire [11:0] IR_q, ram_1_data_3;
  wire [15:0] alu_1_result, multiplexer_1_out, multiplexer_2_out, multiplexer_3_out, multiplexer_4_out,
       pc_1_pc, regbank_1__1, regbank_1__2, regbank_1__3;
  wire [15:4] regbank_1__0_2;

  Clock clock_1 (.out(clock_1_out));
  PC pc_1 (.pc(pc_1_pc), .PC_INC(controlunit_1_pcinc), .clk(clock_1_out));
  RAM #(.addrWidth(16), .dataWidth(16), .bus("separate")) ram_1 (
    .addr(pc_1_pc), .data({ram_1_data_2, ram_1_data, ram_1_data_3}), .str(1'b0), .clk(clock_1_out), .ld(1'b1));  // open: din, sel, clr
  regbank regbank_1 (
    .LD(controlunit_1_ld), .REGSEL(IR_q[1:0]), .Din(multiplexer_1_out), ._0({regbank_1__0_2, regbank_1__0}),
    ._1(regbank_1__1), ._2(regbank_1__2), ._3(regbank_1__3), .clock(clock_1_out));
  Multiplexer #(.width(16), .enable("false")) multiplexer_1 (
    .in0(alu_1_result), .in1({ram_1_data_2, ram_1_data, ram_1_data_3}), .out(multiplexer_1_out),
    .sel(controlunit_1_mux));
  Hex_Digit_Display hex_digit_display_1 (.value(regbank_1__0));  // open: dp
  Hex_Digit_Display hex_digit_display_2 (.value(regbank_1__0_2[7:4]));  // open: dp
  Multiplexer #(.select(2), .width(16), .enable("false")) multiplexer_2 (
    .in0({regbank_1__0_2, regbank_1__0}), .in1(regbank_1__1), .in2(regbank_1__2), .in3(regbank_1__3),
    .out(multiplexer_2_out), .sel(IR_q[7:6]));
  Hex_Digit_Display hex_digit_display_3 (.value(regbank_1__0_2[15:12]));  // open: dp
  Hex_Digit_Display hex_digit_display_4 (.value(regbank_1__0_2[11:8]));  // open: dp
  Multiplexer #(.select(2), .width(16), .enable("false")) multiplexer_3 (
    .in0({regbank_1__0_2, regbank_1__0}), .in1(regbank_1__1), .in2(regbank_1__2), .in3(regbank_1__3),
    .out(multiplexer_3_out), .sel(IR_q[4:3]));
  Multiplexer #(.width(16), .enable("false")) multiplexer_4 (
    .in0(multiplexer_3_out), .in1({ram_1_data_2, ram_1_data, ram_1_data_3}), .out(multiplexer_4_out),
    .sel(controlunit_1_imm));
  ALU alu_1 (
    .inputData1(multiplexer_2_out), .inputData2(multiplexer_4_out), .RESULT(alu_1_result), .ALUOP(IR_q[11:8]));  // open: ZF
  Register #(.width(12)) IR (.D(ram_1_data_3), .en(controlunit_1_irld), .Q(IR_q), .clk(clock_1_out));  // open: clr
  ControlUnit controlunit_1 (
    .Opcode(ram_1_data), .clk(clock_1_out), .IMM(controlunit_1_imm), .PCINC(controlunit_1_pcinc),
    .LD(controlunit_1_ld), .MUX(controlunit_1_mux), .IRLD(controlunit_1_irld));
endmodule

module regbank (
  input  LD,
  input  [1:0] REGSEL,
  input  [15:0] Din,
  input  clock,
  output [15:0] _0,
  output [15:0] _1,
  output [15:0] _2,
  output [15:0] _3
);

  wire and_1_out, and_2_out, and_3_out, and_4_out, decoder_1_out0, decoder_1_out1, decoder_1_out2,
       decoder_1_out3;

  Decoder #(.select(2)) decoder_1 (
    .out0(decoder_1_out0), .out1(decoder_1_out1), .out2(decoder_1_out2), .out3(decoder_1_out3), .sel(REGSEL));  // open: en
  and and_1 (and_1_out, decoder_1_out0, LD);
  and and_2 (and_2_out, decoder_1_out1, LD);
  and and_3 (and_3_out, decoder_1_out2, LD);
  and and_4 (and_4_out, decoder_1_out3, LD);
  Register #(.width(16)) register_1 (.D(Din), .en(and_1_out), .Q(_0), .clk(clock));  // open: clr
  Register #(.width(16)) register_2 (.D(Din), .en(and_2_out), .Q(_1), .clk(clock));  // open: clr
  Register #(.width(16)) register_3 (.D(Din), .en(and_3_out), .Q(_2), .clk(clock));  // open: clr
  Register #(.width(16)) register_4 (.D(Din), .en(and_4_out), .Q(_3), .clk(clock));  // open: clr
endmodule

module ALU (
  input  [15:0] inputData1,
  input  [15:0] inputData2,
  input  [3:0] ALUOP,
  output ZF,
  output [15:0] RESULT
);

  wire [15:0] adder_1_out, adder_2_out, and_1_out, not_1_out, or_1_out, subtractor_1_out, subtractor_2_out,
       xor_1_out;

  Adder #(.width(16)) adder_1 (.a(inputData1), .b(inputData2), .out(adder_1_out));  // open: cin, cout
  Subtractor #(.width(16)) subtractor_1 (.a(inputData1), .b(inputData2), .out(subtractor_1_out));  // open: bin, bout
  assign and_1_out = inputData1 & inputData2;  // AND_Gate and_1, 16 bits wide
  assign or_1_out = inputData1 | inputData2;  // OR_Gate or_1, 16 bits wide
  assign xor_1_out = inputData1 ^ inputData2;  // XOR_Gate xor_1, 16 bits wide
  assign not_1_out = ~inputData1;  // NOT_Gate not_1, 16 bits wide
  Adder #(.width(16)) adder_2 (.a(inputData1), .b(16'h1), .out(adder_2_out));  // open: cin, cout
  Subtractor #(.width(16)) subtractor_2 (.a(inputData1), .b(16'h1), .out(subtractor_2_out));  // open: bin, bout
  Multiplexer #(.select(4), .width(16), .enable("false")) multiplexer_1 (
    .in0(adder_1_out), .in1(subtractor_1_out), .in2(and_1_out), .in3(or_1_out), .in4(xor_1_out),
    .in5(not_1_out), .in6(inputData1), .in7(adder_2_out), .in8(subtractor_2_out), .out(RESULT), .sel(ALUOP));  // open: in9, in10, in11, in12, in13, in14, in15
  nor nor_1 (ZF, RESULT[0], RESULT[1], RESULT[2], RESULT[3], RESULT[4], RESULT[5], RESULT[6], RESULT[7], RESULT[8], RESULT[9], RESULT[10], RESULT[11], RESULT[12], RESULT[13], RESULT[14], RESULT[15]);
endmodule

module PC (
  input  PC_INC,
  input  clk,
  output [15:0] pc
);

  wire [15:0] adder_1_out, multiplexer_1_out;

  Multiplexer #(.width(16), .enable("false")) multiplexer_1 (
    .in0(pc), .in1(adder_1_out), .out(multiplexer_1_out), .sel(PC_INC));
  Register #(.width(16)) u_PC (.D(multiplexer_1_out), .Q(pc), .clk(clk));  // open: en, clr
  Adder #(.width(16)) adder_1 (.a(pc), .b(16'h1), .out(adder_1_out));  // open: cin, cout
endmodule

module ControlUnit (
  input  [1:0] Opcode,
  input  clk,
  output IMM,
  output PCINC,
  output LD,
  output MUX,
  output IRLD
);

  wire [1:0] multiplexer_1_out, register_1_q;
  wire [5:5] rom_1_data;

  Multiplexer #(.width(2), .enable("false")) multiplexer_1 (
    .in0(2'b00), .in1(Opcode), .out(multiplexer_1_out), .sel(rom_1_data[5]));
  Register #(.width(2)) register_1 (.D(multiplexer_1_out), .Q(register_1_q), .clk(clk));  // open: en, clr
  ROM #(.addrWidth(2), .dataWidth(6)) rom_1 (
    .addr(register_1_q), .data({rom_1_data[5], IRLD, MUX, LD, PCINC, IMM}));  // open: sel

  // Notes on the sheet:
  //   contents of rom_1 (hex, n*v repeats v):
  //   32 4 e 7
endmodule
