// Logisim project microProcessor_reptile.circ as structural Verilog: 6 circuits, main circuit main
module main (
  input  [15:0] Key_1,
  input  Ready_1,
  input  [15:0] Key_2,
  input  Ready_2
);

  wire clock_1_out, cpu_1_memld;
  wire [11:0] cpu_1_addrout;
  wire [15:0] cpu_1_dout, ram_1_data;

  Clock clock_1 (.out(clock_1_out));
  CPU cpu_1 (.MEMLD(cpu_1_memld), .clk(clock_1_out), .ADDROUT(cpu_1_addrout), .Dout(cpu_1_dout), .Din(ram_1_data));
  RAM #(.addrWidth(12), .dataWidth(16), .bus("separate")) ram_1 (
    .addr(cpu_1_addrout), .din(cpu_1_dout), .data(ram_1_data), .str(cpu_1_memld), .clk(clock_1_out), .ld(1'b1));  // open: sel, clr
endmodule

module regbank (
  input  REGLD,
  input  [2:0] REGSEL,
  input  [15:0] Din,
  input  clock,
  output [15:0] _0,
  output [15:0] _1,
  output [15:0] _2,
  output [15:0] _3,
  output [15:0] _4,
  output [15:0] _5,
  output [15:0] _6,
  output [15:0] _7
);

  wire and_1_out, and_2_out, and_3_out, and_4_out, and_5_out, and_6_out, and_7_out, and_8_out,
       decoder_1_out0, decoder_1_out1, decoder_1_out2, decoder_1_out3, decoder_1_out4, decoder_1_out5,
       decoder_1_out6, decoder_1_out7;

  Decoder #(.select(3)) decoder_1 (
    .out0(decoder_1_out0), .out1(decoder_1_out1), .out2(decoder_1_out2), .out3(decoder_1_out3),
    .out4(decoder_1_out4), .out5(decoder_1_out5), .out6(decoder_1_out6), .out7(decoder_1_out7), .sel(REGSEL));  // open: en
  and and_1 (and_1_out, decoder_1_out0, REGLD);
  and and_2 (and_2_out, decoder_1_out1, REGLD);
  and and_3 (and_3_out, decoder_1_out2, REGLD);
  and and_4 (and_4_out, decoder_1_out3, REGLD);
  and and_5 (and_5_out, decoder_1_out4, REGLD);
  and and_6 (and_6_out, decoder_1_out5, REGLD);
  and and_7 (and_7_out, decoder_1_out6, REGLD);
  and and_8 (and_8_out, decoder_1_out7, REGLD);
  Register #(.width(16)) register_1 (.D(Din), .en(and_1_out), .Q(_0), .clk(clock));  // open: clr
  Register #(.width(16)) register_2 (.D(Din), .en(and_2_out), .Q(_1), .clk(clock));  // open: clr
  Register #(.width(16)) register_3 (.D(Din), .en(and_3_out), .Q(_2), .clk(clock));  // open: clr
  Register #(.width(16)) register_4 (.D(Din), .en(and_4_out), .Q(_3), .clk(clock));  // open: clr
  Register #(.width(16)) register_5 (.D(Din), .en(and_5_out), .Q(_4), .clk(clock));  // open: clr
  Register #(.width(16)) register_6 (.D(Din), .en(and_6_out), .Q(_5), .clk(clock));  // open: clr
  Register #(.width(16)) register_7 (.D(Din), .en(and_7_out), .Q(_6), .clk(clock));  // open: clr
  Register #(.width(16)) register_8 (.D(Din), .en(and_8_out), .Q(_7), .clk(clock));  // open: clr
endmodule

module ALU (
  input  [15:0] inputData1,
  input  [15:0] inputData2,
  input  [5:0] ALUOP,
  output ZF,
  output [15:0] RESULT
);

  wire [15:0] adder_1_out, adder_2_out, and_1_out, multiplexer_1_out, not_1_out, or_1_out, subtractor_1_out,
       subtractor_2_out, xor_1_out;

  Adder #(.width(16)) adder_1 (.a(inputData1), .b(inputData2), .out(adder_1_out));  // open: cin, cout
  Subtractor #(.width(16)) subtractor_1 (.a(inputData1), .b(inputData2), .out(subtractor_1_out));  // open: bin, bout
  assign and_1_out = inputData1 & inputData2;  // AND_Gate and_1, 16 bits wide
  assign or_1_out = inputData1 | inputData2;  // OR_Gate or_1, 16 bits wide
  assign xor_1_out = inputData1 ^ inputData2;  // XOR_Gate xor_1, 16 bits wide
  assign not_1_out = ~inputData1;  // NOT_Gate not_1, 16 bits wide
  Adder #(.width(16)) adder_2 (.a(inputData1), .b(16'h1), .out(adder_2_out));  // open: cin, cout
  Subtractor #(.width(16)) subtractor_2 (.a(inputData1), .b(16'h1), .out(subtractor_2_out));  // open: bin, bout
  Multiplexer #(.select(3), .width(16), .enable("false")) multiplexer_1 (
    .in0(not_1_out), .in1(inputData1), .in2(adder_2_out), .in3(subtractor_2_out), .out(multiplexer_1_out),
    .sel(ALUOP[2:0]));  // open: in4, in5, in6, in7
  Multiplexer #(.select(3), .width(16), .enable("false")) multiplexer_2 (
    .in0(adder_1_out), .in1(subtractor_1_out), .in2(and_1_out), .in3(or_1_out), .in4(xor_1_out),
    .in7(multiplexer_1_out), .out(RESULT), .sel(ALUOP[5:3]));  // open: in5, in6
  nor nor_1 (ZF, RESULT[0], RESULT[1], RESULT[2], RESULT[3], RESULT[4], RESULT[5], RESULT[6], RESULT[7], RESULT[8], RESULT[9], RESULT[10], RESULT[11], RESULT[12], RESULT[13], RESULT[14], RESULT[15]);
endmodule

module PC (
  input  PCLD,
  input  PC_INC,
  input  [11:0] JUMPADDR,
  input  clk,
  output [11:0] pc
);

  wire [11:0] adder_1_out, multiplexer_1_out, multiplexer_2_out;

  Multiplexer #(.width(12), .enable("false")) multiplexer_1 (
    .in0(pc), .in1(adder_1_out), .out(multiplexer_1_out), .sel(PC_INC));
  Multiplexer #(.width(12), .enable("false")) multiplexer_2 (
    .in0(multiplexer_1_out), .in1(JUMPADDR), .out(multiplexer_2_out), .sel(PCLD));
  Register #(.width(12)) u_PC (.D(multiplexer_2_out), .Q(pc), .clk(clk));  // open: en, clr
  Adder #(.width(12)) adder_1 (.a(pc), .b(12'h1), .out(adder_1_out));  // open: cin, cout
endmodule

module ControlUnit (
  input  [3:0] opcode,
  input  ZF,
  input  clk,
  output IMM,
  output IRLD,
  output MEMLD,
  output MUX,
  output ZFLD,
  output REGLD,
  output ADRMUX,
  output PCINC,
  output PCLD
);

  wire not_1_out, not_2_out;
  wire [1:1] and_1_out;
  wire [2:0] multiplexer_1_out, multiplexer_2_out, register_1_q;
  wire [9:9] rom_1_data;

  and and_1 (and_1_out[1], not_1_out, not_2_out, opcode[2]);
  not not_1 (not_1_out, opcode[0]);
  not not_2 (not_2_out, opcode[1]);
  Multiplexer #(.select(2), .width(3), .enable("false")) multiplexer_1 (
    .in0(opcode[2:0]), .in1(opcode[2:0]), .in2(3'b000), .in3(3'b101), .out(multiplexer_1_out),
    .sel({and_1_out[1], ZF}));
  Multiplexer #(.width(3), .enable("false")) multiplexer_2 (
    .in0(3'b000), .in1(multiplexer_1_out), .out(multiplexer_2_out), .sel(rom_1_data[9]));
  Register #(.width(3)) register_1 (.D(multiplexer_2_out), .Q(register_1_q), .clk(clk));  // open: en, clr
  ROM #(.addrWidth(3), .dataWidth(10)) rom_1 (
    .addr(register_1_q), .data({rom_1_data[9], PCLD, PCINC, ADRMUX, REGLD, ZFLD, MUX, MEMLD, IRLD, IMM}));  // open: sel

  // Notes on the sheet:
  //   contents of rom_1 (hex, n*v repeats v):
  //   282 a8 68 44 0 100 b1 30
endmodule

module CPU (
  input  [15:0] Din,
  input  clk,
  output [11:0] ADDROUT,
  output [15:0] Dout,
  output MEMLD
);

  wire alu_1_zf, controlunit_1_adrmux, controlunit_1_imm, controlunit_1_irld, controlunit_1_mux,
       controlunit_1_pcinc, controlunit_1_pcld, controlunit_1_regld, controlunit_1_zfld, ZF_q;
  wire [2:0] IR_q, IR_q_3;
  wire [11:0] adder_1_out, multiplexer_4_out, pc_1_pc;
  wire [11:3] IR_q_2;
  wire [15:0] alu_1_result, multiplexer_2_out, multiplexer_5_out, regbank_1__0, regbank_1__1, regbank_1__2,
       regbank_1__3, regbank_1__4, regbank_1__5, regbank_1__6, regbank_1__7;
  wire [15:12] multiplexer_4_out_2;

  PC pc_1 (.pc(pc_1_pc), .PC_INC(controlunit_1_pcinc), .clk(clk), .PCLD(controlunit_1_pcld), .JUMPADDR(adder_1_out));
  Adder #(.width(12)) adder_1 (
    .a(pc_1_pc), .b({IR_q_2[11:9], IR_q_3, IR_q_2[5:3], IR_q}), .out(adder_1_out));  // open: cin, cout
  Multiplexer #(.width(12), .enable("false")) multiplexer_1 (
    .in0(pc_1_pc), .in1(multiplexer_4_out), .out(ADDROUT), .sel(controlunit_1_adrmux));
  regbank regbank_1 (
    .REGLD(controlunit_1_regld), .REGSEL(IR_q), .Din(multiplexer_2_out), ._0(regbank_1__0),
    ._1(regbank_1__1), ._2(regbank_1__2), ._3(regbank_1__3), .clock(clk), ._4(regbank_1__4),
    ._5(regbank_1__5), ._6(regbank_1__6), ._7(regbank_1__7));
  Multiplexer #(.width(16), .enable("false")) multiplexer_2 (
    .in0(alu_1_result), .in1(Din), .out(multiplexer_2_out), .sel(controlunit_1_mux));
  Multiplexer #(.select(3), .width(16), .enable("false")) multiplexer_3 (
    .in0(regbank_1__0), .in1(regbank_1__1), .in2(regbank_1__2), .in3(regbank_1__3), .in4(regbank_1__4),
    .in5(regbank_1__5), .in6(regbank_1__6), .in7(regbank_1__7), .out(Dout), .sel(IR_q_2[5:3]));
  Multiplexer #(.select(3), .width(16), .enable("false")) multiplexer_4 (
    .in0(regbank_1__0), .in1(regbank_1__1), .in2(regbank_1__2), .in3(regbank_1__3), .in4(regbank_1__4),
    .in5(regbank_1__5), .in6(regbank_1__6), .in7(regbank_1__7),
    .out({multiplexer_4_out_2, multiplexer_4_out}), .sel(IR_q_3));
  Multiplexer #(.width(16), .enable("false")) multiplexer_5 (
    .in0({multiplexer_4_out_2, multiplexer_4_out}), .in1(Din), .out(multiplexer_5_out),
    .sel(controlunit_1_imm));
  ALU alu_1 (
    .inputData1(Dout), .inputData2(multiplexer_5_out), .ZF(alu_1_zf), .RESULT(alu_1_result),
    .ALUOP({IR_q_2[11:9], IR_q_3}));
  Register #(.width(1)) ZF (.D(alu_1_zf), .en(controlunit_1_zfld), .Q(ZF_q), .clk(clk));  // open: clr
  Register #(.width(12)) IR (
    .D(Din[11:0]), .en(controlunit_1_irld), .Q({IR_q_2[11:9], IR_q_3, IR_q_2[5:3], IR_q}), .clk(clk));  // open: clr
  ControlUnit controlunit_1 (
    .ZF(ZF_q), .IMM(controlunit_1_imm), .IRLD(controlunit_1_irld), .MEMLD(MEMLD), .MUX(controlunit_1_mux),
    .ZFLD(controlunit_1_zfld), .REGLD(controlunit_1_regld), .ADRMUX(controlunit_1_adrmux),
    .PCINC(controlunit_1_pcinc), .PCLD(controlunit_1_pcld), .opcode(Din[15:12]), .clk(clk));
endmodule
